# Fritzing sketch ARC (saved by Fritzing 0.9.3b)
circuit board: 8.46667cm x 5.64444cm

parts:
  Screen = Grove OLED 128x96
  OK = Pushbutton [package="[SMD]"]
  Prev = Pushbutton [package="[SMD]"]
  Next = Pushbutton [package="[SMD]"]
  U1 = LuaNode32 / ESP32 [part_number=ESP32S-PIN30]

nets:
  GND: Screen.GND, Prev.Pin_3, Prev.Pin_4, Next.Pin_3, Next.Pin_4, U1.GND
  VCC: Screen.VCC, U1.3V3
  N1: Screen.SDA, U1.D21
  N2: Screen.SCL, U1.D22
  N3: OK.Pin_1, OK.Pin_2, U1.Vin
  N4: OK.Pin_3, U1.D18
  N5: Prev.Pin_1, Prev.Pin_2, U1.D4
  N6: Next.Pin_1, Next.Pin_2, U1.D2

custom parts:
  LuaNode32 / ESP32: New Image for LuaNode32 DOIT ESP32 DEVKIT V1. Base parts from LuaNode32 / ESP32 ESP32 based LuaNode32 by G.Noorlander DOIT Esp32 DevKit v1 (30 pins long, 11 pins width) by Werner Rothschopf (modified by vanepp Dec 2018)
